// Logisim project Circuit.circ as structural Verilog: 5 circuits, main circuit main
module main (
  input  B0,
  input  B1,
  input  B2,
  input  B3,
  input  B4,
  input  B5,
  input  B6,
  input  B7,
  input  A0,
  input  A1,
  input  A2,
  input  A3,
  input  A4,
  input  A5,
  input  A6,
  input  A7
);

  wire [7:0] eightbit2compliment_2_o0, multiplexer_1_out;

  Button Start ();  // open: out
  eightbit2compliment eightbit2compliment_1 ();  // open: I7, I6, I5, I4, I3, I2, I1, I0, O0, O7, O6, O5, O4, O3, O2, O1
  eightbit2compliment eightbit2compliment_2 (
    .I7(B7), .I6(B6), .I5(B5), .I4(B4), .I3(B3), .I2(B2), .I1(B1), .I0(B0), .O0(eightbit2compliment_2_o0[0]),
    .O7(eightbit2compliment_2_o0[7]), .O6(eightbit2compliment_2_o0[6]), .O5(eightbit2compliment_2_o0[5]),
    .O4(eightbit2compliment_2_o0[4]), .O3(eightbit2compliment_2_o0[3]), .O2(eightbit2compliment_2_o0[2]),
    .O1(eightbit2compliment_2_o0[1]));
  // XOR_Gate xor_1 has open pins: in0=A7, in1=B7, out=open
  Multiplexer multiplexer_1 (.in0(B0), .in1(eightbit2compliment_2_o0[0]), .out(multiplexer_1_out[0]), .sel(B7));
  // Pins of 1 and 8 bits meet at {B7, B6, B5, B4, B3, B2, B1, B0}
  // Pins of 1 and 8 bits meet at eightbit2compliment_2_o0
  // Pins of 1 and 8 bits meet at multiplexer_1_out
endmodule

module eightbit2compliment (
  input  I0,
  input  I1,
  input  I2,
  input  I3,
  input  I4,
  input  I5,
  input  I6,
  input  I7,
  output O0,
  output O1,
  output O2,
  output O3,
  output O4,
  output O5,
  output O6,
  output O7
);

  wire adder_2_cout, adder_3_cout, adder_4_cout, adder_5_cout, adder_6_cout, adder_7_cout, adder_8_cout,
       not_1_out, not_2_out, not_3_out, not_4_out, not_5_out, not_6_out, not_7_out, not_8_out;

  not not_1 (not_1_out, I7);
  not not_2 (not_2_out, I6);
  Adder #(.width(1)) adder_1 (.a(not_1_out), .b(adder_2_cout), .out(O7));  // open: cin, cout
  not not_3 (not_3_out, I5);
  Adder #(.width(1)) adder_2 (.a(not_2_out), .b(adder_3_cout), .out(O6), .cout(adder_2_cout));  // open: cin
  not not_4 (not_4_out, I4);
  Adder #(.width(1)) adder_3 (.a(not_3_out), .b(adder_4_cout), .out(O5), .cout(adder_3_cout));  // open: cin
  Adder #(.width(1)) adder_4 (.a(not_4_out), .b(adder_5_cout), .out(O4), .cout(adder_4_cout));  // open: cin
  not not_5 (not_5_out, I3);
  Adder #(.width(1)) adder_5 (.a(not_5_out), .b(adder_6_cout), .out(O3), .cout(adder_5_cout));  // open: cin
  not not_6 (not_6_out, I2);
  Adder #(.width(1)) adder_6 (.a(not_6_out), .b(adder_7_cout), .out(O2), .cout(adder_6_cout));  // open: cin
  not not_7 (not_7_out, I1);
  Adder #(.width(1)) adder_7 (.a(not_7_out), .b(adder_8_cout), .out(O1), .cout(adder_7_cout));  // open: cin
  not not_8 (not_8_out, I0);
  Adder #(.width(1)) adder_8 (.a(not_8_out), .b(1'b1), .out(O0), .cout(adder_8_cout));  // open: cin
endmodule

// reg
module shiftRightReg (
  input  i_0,
  input  i_1,
  input  i_2,
  input  i_3,
  input  i_4,
  input  i_5,
  input  i_6,
  input  i_7,
  input  Clock,
  input  Enable,
  input  Load,
  output O0,
  output O1,
  output O2,
  output O3,
  output O4,
  output O5,
  output O6,
  output O7
);

  wire multiplexer_1_out, multiplexer_2_out, multiplexer_3_out, multiplexer_4_out, multiplexer_5_out,
       multiplexer_6_out, multiplexer_7_out, multiplexer_8_out, multiplexer_9_out, multiplexer_10_out,
       multiplexer_11_out, multiplexer_12_out, multiplexer_13_out, multiplexer_14_out, multiplexer_15_out,
       multiplexer_16_out, undriven, undriven_2, undriven_3, undriven_4, undriven_5, undriven_6, undriven_7,
       undriven_8;

  Multiplexer multiplexer_1 (.in0(1'b0), .in1(i_0), .out(multiplexer_1_out), .sel(Load));
  D_Flip_Flop d_ff_1 (.D(multiplexer_2_out), .clk(Clock), .Q(O0), .reset(undriven));  // open: Qn, preset
  Multiplexer multiplexer_2 (.in0(O0), .in1(multiplexer_1_out), .out(multiplexer_2_out), .sel(Enable));
  D_Flip_Flop d_ff_2 ();  // open: D, clk, Q, Qn, preset, reset
  Multiplexer multiplexer_3 (.in0(O0), .in1(i_1), .out(multiplexer_3_out), .sel(Load));
  D_Flip_Flop d_ff_3 (.D(multiplexer_4_out), .clk(Clock), .Q(O1), .reset(undriven_2));  // open: Qn, preset
  Multiplexer multiplexer_4 (.in0(O1), .in1(multiplexer_3_out), .out(multiplexer_4_out), .sel(Enable));
  Multiplexer multiplexer_5 (.in0(O2), .in1(multiplexer_6_out), .out(multiplexer_5_out), .sel(Enable));
  Multiplexer multiplexer_6 (.in0(O1), .in1(i_2), .out(multiplexer_6_out), .sel(Load));
  D_Flip_Flop d_ff_4 (.D(multiplexer_5_out), .clk(Clock), .Q(O2), .reset(undriven_3));  // open: Qn, preset
  Multiplexer multiplexer_7 (.in0(O2), .in1(i_3), .out(multiplexer_7_out), .sel(Load));
  D_Flip_Flop d_ff_5 (.D(multiplexer_8_out), .clk(Clock), .Q(O3), .reset(undriven_4));  // open: Qn, preset
  Multiplexer multiplexer_8 (.in0(O3), .in1(multiplexer_7_out), .out(multiplexer_8_out), .sel(Enable));
  Multiplexer multiplexer_9 (.in0(O3), .in1(i_4), .out(multiplexer_9_out), .sel(Load));
  Multiplexer multiplexer_10 (.in0(O4), .in1(multiplexer_9_out), .out(multiplexer_10_out), .sel(Enable));
  D_Flip_Flop d_ff_6 (.D(multiplexer_10_out), .clk(Clock), .Q(O4), .reset(undriven_5));  // open: Qn, preset
  Multiplexer multiplexer_11 (.in0(O4), .in1(i_5), .out(multiplexer_11_out), .sel(Load));
  Multiplexer multiplexer_12 (.in0(O5), .in1(multiplexer_11_out), .out(multiplexer_12_out), .sel(Enable));
  D_Flip_Flop d_ff_7 (.D(multiplexer_12_out), .clk(Clock), .Q(O5), .reset(undriven_6));  // open: Qn, preset
  Multiplexer multiplexer_13 (.in0(O5), .in1(i_6), .out(multiplexer_13_out), .sel(Load));
  Multiplexer multiplexer_14 (.in0(O6), .in1(multiplexer_13_out), .out(multiplexer_14_out), .sel(Enable));
  D_Flip_Flop d_ff_8 (.D(multiplexer_14_out), .clk(Clock), .Q(O6), .reset(undriven_7));  // open: Qn, preset
  Multiplexer multiplexer_15 (.in0(O6), .in1(i_7), .out(multiplexer_15_out), .sel(Load));
  Multiplexer multiplexer_16 (.in0(O7), .in1(multiplexer_15_out), .out(multiplexer_16_out), .sel(Enable));
  D_Flip_Flop d_ff_9 (.D(multiplexer_16_out), .clk(Clock), .Q(O7), .reset(undriven_8));  // open: Qn, preset
endmodule

module shiftLeftReg (
  input  i_0,
  input  i_1,
  input  i_2,
  input  i_3,
  input  i_4,
  input  i_5,
  input  i_6,
  input  i_7,
  input  Clock,
  input  Enable,
  input  Load,
  output out_12
);

  wire d_ff_2_q, d_ff_3_q, d_ff_4_q, d_ff_5_q, d_ff_6_q, d_ff_7_q, d_ff_8_q, multiplexer_1_out,
       multiplexer_2_out, multiplexer_3_out, multiplexer_4_out, multiplexer_5_out, multiplexer_6_out,
       multiplexer_7_out, multiplexer_8_out, multiplexer_9_out, multiplexer_10_out, multiplexer_11_out,
       multiplexer_12_out, multiplexer_13_out, multiplexer_14_out, multiplexer_15_out, multiplexer_16_out,
       undriven, undriven_2, undriven_3, undriven_4, undriven_5, undriven_6, undriven_7, undriven_8;

  Multiplexer multiplexer_1 (.in0(d_ff_2_q), .in1(i_0), .out(multiplexer_1_out), .sel(Load));
  D_Flip_Flop d_ff_1 (.D(multiplexer_2_out), .clk(Clock), .Q(out_12), .reset(undriven));  // open: Qn, preset
  Multiplexer multiplexer_2 (.in0(out_12), .in1(multiplexer_1_out), .out(multiplexer_2_out), .sel(Enable));
  LED led_1 (.in(out_12));
  Multiplexer multiplexer_3 (.in0(d_ff_3_q), .in1(i_1), .out(multiplexer_3_out), .sel(Load));
  D_Flip_Flop d_ff_2 (.D(multiplexer_4_out), .clk(Clock), .Q(d_ff_2_q), .reset(undriven_2));  // open: Qn, preset
  Multiplexer multiplexer_4 (.in0(d_ff_2_q), .in1(multiplexer_3_out), .out(multiplexer_4_out), .sel(Enable));
  Multiplexer multiplexer_5 (.in0(d_ff_3_q), .in1(multiplexer_6_out), .out(multiplexer_5_out), .sel(Enable));
  Multiplexer multiplexer_6 (.in0(d_ff_4_q), .in1(i_2), .out(multiplexer_6_out), .sel(Load));
  D_Flip_Flop d_ff_3 (.D(multiplexer_5_out), .clk(Clock), .Q(d_ff_3_q), .reset(undriven_3));  // open: Qn, preset
  Multiplexer multiplexer_7 (.in0(d_ff_5_q), .in1(i_3), .out(multiplexer_7_out), .sel(Load));
  D_Flip_Flop d_ff_4 (.D(multiplexer_8_out), .clk(Clock), .Q(d_ff_4_q), .reset(undriven_4));  // open: Qn, preset
  Multiplexer multiplexer_8 (.in0(d_ff_4_q), .in1(multiplexer_7_out), .out(multiplexer_8_out), .sel(Enable));
  Multiplexer multiplexer_9 (.in0(d_ff_6_q), .in1(i_4), .out(multiplexer_9_out), .sel(Load));
  Multiplexer multiplexer_10 (.in0(d_ff_5_q), .in1(multiplexer_9_out), .out(multiplexer_10_out), .sel(Enable));
  D_Flip_Flop d_ff_5 (.D(multiplexer_10_out), .clk(Clock), .Q(d_ff_5_q), .reset(undriven_5));  // open: Qn, preset
  Multiplexer multiplexer_11 (.in0(d_ff_7_q), .in1(i_5), .out(multiplexer_11_out), .sel(Load));
  Multiplexer multiplexer_12 (.in0(d_ff_6_q), .in1(multiplexer_11_out), .out(multiplexer_12_out), .sel(Enable));
  D_Flip_Flop d_ff_6 (.D(multiplexer_12_out), .clk(Clock), .Q(d_ff_6_q), .reset(undriven_6));  // open: Qn, preset
  Multiplexer multiplexer_13 (.in0(d_ff_8_q), .in1(i_6), .out(multiplexer_13_out), .sel(Load));
  Multiplexer multiplexer_14 (.in0(d_ff_7_q), .in1(multiplexer_13_out), .out(multiplexer_14_out), .sel(Enable));
  D_Flip_Flop d_ff_7 (.D(multiplexer_14_out), .clk(Clock), .Q(d_ff_7_q), .reset(undriven_7));  // open: Qn, preset
  Multiplexer multiplexer_15 (.in0(1'b0), .in1(i_7), .out(multiplexer_15_out), .sel(Load));
  Multiplexer multiplexer_16 (.in0(d_ff_8_q), .in1(multiplexer_15_out), .out(multiplexer_16_out), .sel(Enable));
  D_Flip_Flop d_ff_8 (.D(multiplexer_16_out), .clk(Clock), .Q(d_ff_8_q), .reset(undriven_8));  // open: Qn, preset
endmodule

module ControlUnit (
  input  B0,
  input  Z,
  input  Load,
  output Psel,
  output EP,
  output EA,
  output EB,
  output LA,
  output LB,
  output RstP
);

  wire not_2_out;

  not not_1 (EA, Z);
  not not_2 (not_2_out, Load);
  and and_1 (EP, B0, not_2_out);

  assign EB = EA;
  assign LA = Load;
  assign LB = Load;
  assign Psel = B0;
  assign RstP = Load;
endmodule
